# Fritzing sketch Sketch (saved by Fritzing 0.9.4)
breadboards: 1

parts:
  U1 = ESP8266 NodeMCU LoLin module
  Bauteil1 = LCD Keypad Shield  # not connected
  R1 = Resistor [tolerance=±5% resistance=4.7k package="1206 [SMD]"]
  R2 = Resistor [tolerance=±5% resistance=4.7k package="1206 [SMD]"]
  R3 = Resistor [tolerance=±5% resistance=4.7k package="1206 [SMD]"]
  R4 = Resistor [tolerance=±5% resistance=4.7k package="1206 [SMD]"]

nets:
  N1: U1.A0, R1.Pin_1, R2.Pin_0
  N2: R2.Pin_1, R3.Pin_0
  N3: R3.Pin_1, R4.Pin_0

notes:
  Voltage divider from 4.7V to approx. 1.1V (max. Input-Voltage for A0 on ESP8266)

custom parts:
  ESP8266 NodeMCU LoLin module: ESP8266 based NodeMCU
  LCD Keypad Shield: It consists of a 1602 white character blue backlight LCD. The keypad consists of 5 keys — select, up, right, down and left. To save the digital IO pins, the keypad interface uses only one ADC channel. The key value is read through a 5 stage voltage divider.
